# Fritzing sketch Robo Resenha (saved by Fritzing 1.0.2b)

parts:
  Componente1 = Arduino Uno (Rev3) - ICSP  # not connected
  Palpebra_dir = Basic Servo
  Palpebra_esq = Basic Servo
  Olho_dir = Basic Servo
  Olho_esq = Basic Servo
  Sobrancelha_dir = Basic Servo
  Sobrancelha_esq = Basic Servo
  Boca_dir = Basic Servo
  Boca_esq = Basic Servo
  Mod1 = Arduino Sensor Shield v5.0

nets:
  GND: Palpebra_dir.gnd, Palpebra_esq.gnd, Olho_dir.gnd, Olho_esq.gnd, Sobrancelha_dir.gnd, Sobrancelha_esq.gnd, Boca_dir.gnd, Boca_esq.gnd, Mod1.URF01-GND, Mod1.GND, Mod1.BLUETOOTH-GND, Mod1.7-G, Mod1.6-G, Mod1.5-G, Mod1.4-G, Mod1.3-G, Mod1.2-G, Mod1.1-G, Mod1.0-G
  5V: Palpebra_dir.vcc, Palpebra_esq.pulse, Olho_dir.vcc, Olho_esq.vcc, Sobrancelha_dir.vcc, Sobrancelha_esq.vcc, Boca_dir.vcc, Boca_esq.vcc, Mod1.VCC, Mod1.URF01-VCC, Mod1.BLUETOOTH-VCC, Mod1.7-V, Mod1.6-V, Mod1.5-V, Mod1.4-V, Mod1.3-V, Mod1.2-V, Mod1.1-V, Mod1.0-V
  N1: Palpebra_dir.pulse, Mod1.7-S
  N2: Palpebra_esq.vcc, Mod1.5-S
  N3: Olho_dir.pulse, Mod1.6-S
  N4: Olho_esq.pulse, Mod1.4-S, Mod1.SerialLCD-D4
  N5: Sobrancelha_dir.pulse, Mod1.3-S
  N6: Sobrancelha_esq.pulse, Mod1.2-S
  N7: Boca_dir.pulse, Mod1.BLUETOOTH-D1, Mod1.1-S
  N8: Boca_esq.pulse, Mod1.BLUETOOTH-D0, Mod1.0-S
